// Digital circuit instruction_mem.dig as structural Verilog
module instruction_mem (
  input  [31:0] ADDR_32,
  input  Enable_1,
  output [31:0] Out_32
);

  ROM #(.AddrBits(8), .Bits(32)) rom_1 (.A(ADDR_32[7:0]), .sel(Enable_1), .D(Out_32));

  // Notes on the sheet:
  //   contents of rom_1 (hex, n*v repeats v):
  //   4*61616161
endmodule
